// Logisim project 8bitcomputer.circ as structural Verilog: 4 circuits, main circuit main
module main (
  input  in_1,
  input  in_2,
  input  in_3,
  input  in_4,
  input  in_5,
  input  in_6,
  input  in_7,
  input  in_8,
  input  in_9,
  input  in_10,
  input  in_11,
  input  in_12,
  input  in_13,
  output out_14,
  output out_15,
  output out_16,
  output out_17,
  output out_18,
  output out_19,
  output out_20,
  output out_21,
  output out_22,
  output out_23,
  output out_24,
  output out_25,
  output out_26,
  output out_27,
  output out_28,
  output out_29,
  output out_30,
  output out_31,
  output out_32,
  output out_33,
  output out_34,
  output out_35,
  output out_36,
  output out_37
);

  wire clock_1_out, n1bitregister_1_p18;

  assign out_14 = in_1 ? in_2 : 1'bz;  // Controlled_Buffer controlled_buffer_1
  assign out_15 = in_1 ? in_3 : 1'bz;  // Controlled_Buffer controlled_buffer_2
  assign out_16 = in_1 ? in_4 : 1'bz;  // Controlled_Buffer controlled_buffer_3
  assign out_17 = in_1 ? in_5 : 1'bz;  // Controlled_Buffer controlled_buffer_4
  assign out_18 = in_1 ? in_7 : 1'bz;  // Controlled_Buffer controlled_buffer_5
  assign out_19 = in_1 ? in_8 : 1'bz;  // Controlled_Buffer controlled_buffer_6
  assign out_20 = in_1 ? in_9 : 1'bz;  // Controlled_Buffer controlled_buffer_7
  assign out_21 = in_1 ? in_10 : 1'bz;  // Controlled_Buffer controlled_buffer_8
  alu_main alu_main_1 (
    .A0(out_22), .A1(out_23), .A2(out_24), .A3(out_25), .A4(out_26), .A5(out_27), .A6(out_28), .A7(out_29),
    .B0(out_30), .B1(out_31), .B2(out_32), .B3(out_33), .B4(out_34), .B5(out_35), .B6(out_36), .B7(out_37),
    .SUB(in_11), .EN(in_12), .out_19(out_14), .out_20(out_15), .out_21(out_16), .out_22(out_17),
    .out_23(out_18), .out_24(out_19), .out_25(out_20), .out_26(out_21));
  Clock clock_1 (.out(clock_1_out));
  // _1bitregister 1bitregister_1: pin names not known; wires that end beside it: out_14, out_30, out_15, out_31, out_16, out_32, out_17, out_33, out_18, out_34, out_19, out_35, out_20, out_36, out_21, out_37, in_13, n1bitregister_1_p18
  // _1bitregister 1bitregister_2: pin names not known; wires that end beside it: clock_1_out, in_6, out_29, out_21, out_28, out_20, out_27, out_19, out_26, out_18, out_25, out_17, out_24, out_16, out_23, out_15, out_22, out_14
  Clock clock_2 (.out(n1bitregister_1_p18));
endmodule

module full__adder (
  input  A,
  input  B,
  input  Cin,
  output S,
  output Co
);

  wire and_1_out, and_2_out, and_3_out, and_4_out, and_5_out, and_6_out, not_1_out, not_2_out, not_3_out,
       not_4_out, or_1_out;

  not not_1 (not_1_out, B);
  not not_2 (not_2_out, A);
  and and_1 (and_1_out, not_1_out, A);
  and and_2 (and_2_out, B, not_2_out);
  or or_1 (or_1_out, and_1_out, and_2_out);
  and and_3 (and_3_out, A, B);
  not not_3 (not_3_out, Cin);
  not not_4 (not_4_out, or_1_out);
  and and_4 (and_4_out, Cin, or_1_out);
  and and_5 (and_5_out, not_3_out, or_1_out);
  and and_6 (and_6_out, not_4_out, Cin);
  or or_2 (Co, and_4_out, and_3_out);
  or or_3 (S, and_5_out, and_6_out);

  // Notes on the sheet:
  //   A
  //   B
  //   Cin
  //   S
  //   Co
endmodule

module _4_b (
  input  in_1,
  input  in_2,
  input  in_3,
  input  in_4,
  input  in_5,
  input  B0,
  input  in_7,
  input  in_8,
  input  in_9,
  output out_10,
  output out_11,
  output out_12,
  output out_13,
  output out_14
);

  wire and_1_out, and_4_out, and_5_out, and_6_out, and_9_out, and_10_out, and_11_out, and_12_out, and_13_out,
       and_14_out, C0, C1, C2, G0, G1, G2, G3, P0, P1, P2, P3;

  and and_1 (and_1_out, P0, in_5);
  xor xor_1 (P0, in_1, B0);
  xor xor_2 (P1, in_2, in_7);
  and and_2 (G0, in_1, B0);
  and and_3 (G1, in_2, in_7);
  or or_1 (C0, and_1_out, G0);
  and and_4 (and_4_out, in_5, P2, P0, P1);
  and and_5 (and_5_out, P1, P2, G0);
  and and_6 (and_6_out, P2, G1);
  or or_2 (C2, and_4_out, G2, and_6_out, and_5_out);
  xor xor_3 (P2, in_3, in_8);
  xor xor_4 (P3, in_4, in_9);
  and and_7 (G2, in_3, in_8);
  and and_8 (G3, in_4, in_9);
  and and_9 (and_9_out, P0, P1, in_5);
  and and_10 (and_10_out, P1, G0);
  and and_11 (and_11_out, in_5, P0, P1, P2, P3);
  and and_12 (and_12_out, P3, P2, P1, G0);
  and and_13 (and_13_out, P3, P2, G1);
  and and_14 (and_14_out, P3, G2);
  or or_3 (C1, and_9_out, G1, and_10_out);
  or or_4 (out_14, G3, and_11_out, and_12_out, and_13_out, and_14_out);
  full__adder full_adder_1 (.A(in_1), .B(B0), .Cin(in_5), .S(out_10));  // open: Co
  full__adder full_adder_2 (.A(in_4), .B(in_9), .Cin(C2), .S(out_13));  // open: Co
  full__adder full_adder_3 (.A(in_2), .B(in_7), .Cin(C0), .S(out_11));  // open: Co
  full__adder full_adder_4 (.A(in_3), .B(in_8), .Cin(C1), .S(out_12));  // open: Co

  // Other names for the same wires on the sheet: A0 = in_1; A1 = in_2; A2 = in_3; A3 = in_4; B1 = in_7; B2 = in_8;
  //   B3 = in_9; Cin = in_5; Cout = out_14; S0 = out_10; S1 = out_11; S2 = out_12; S3 = out_13

  // Notes on the sheet:
  //   C0
  //   C2
  //   generating variables
  //   C1
  //   Cout
  //   FOR BIT 0
  //   FOR BIT 3
  //   Predicting Carries
  //   Implementation
  //   FOR BIT 1
  //   FOR BIT 2
endmodule

module alu_main (
  input  A0,
  input  A1,
  input  A2,
  input  A3,
  input  A4,
  input  A5,
  input  A6,
  input  A7,
  input  B0,
  input  B1,
  input  B2,
  input  B3,
  input  B4,
  input  B5,
  input  B6,
  input  B7,
  input  SUB,
  input  EN,
  output out_19,
  output out_20,
  output out_21,
  output out_22,
  output out_23,
  output out_24,
  output out_25,
  output out_26
);

  wire n4_b_1_out_10, n4_b_1_out_11, n4_b_1_out_12, n4_b_1_out_13, n4_b_1_out_14, n4_b_2_out_10,
       n4_b_2_out_11, n4_b_2_out_12, n4_b_2_out_13, xor_1_out, xor_2_out, xor_3_out, xor_4_out, xor_5_out,
       xor_6_out, xor_7_out, xor_8_out;

  xor xor_1 (xor_1_out, B0, SUB);
  xor xor_2 (xor_2_out, B1, SUB);
  xor xor_3 (xor_3_out, B2, SUB);
  xor xor_4 (xor_4_out, B3, SUB);
  xor xor_5 (xor_5_out, B4, SUB);
  xor xor_6 (xor_6_out, B5, SUB);
  xor xor_7 (xor_7_out, B6, SUB);
  xor xor_8 (xor_8_out, B7, SUB);
  _4_b u_4_b_1 (
    .in_1(A0), .in_2(A1), .in_3(A2), .in_4(A3), .B0(xor_1_out), .in_7(xor_2_out), .in_8(xor_3_out),
    .in_9(xor_4_out), .out_10(n4_b_1_out_10), .out_11(n4_b_1_out_11), .out_12(n4_b_1_out_12),
    .out_13(n4_b_1_out_13), .out_14(n4_b_1_out_14), .in_5(SUB));
  _4_b u_4_b_2 (
    .in_1(A4), .in_2(A5), .in_3(A6), .in_4(A7), .B0(xor_5_out), .in_7(xor_6_out), .in_8(xor_7_out),
    .in_9(xor_8_out), .out_10(n4_b_2_out_10), .out_11(n4_b_2_out_11), .out_12(n4_b_2_out_12),
    .out_13(n4_b_2_out_13), .in_5(n4_b_1_out_14));  // open: out_14
  assign out_19 = EN ? n4_b_1_out_10 : 1'bz;  // Controlled_Buffer controlled_buffer_1
  assign out_20 = EN ? n4_b_1_out_11 : 1'bz;  // Controlled_Buffer controlled_buffer_2
  assign out_21 = EN ? n4_b_1_out_12 : 1'bz;  // Controlled_Buffer controlled_buffer_3
  assign out_22 = EN ? n4_b_1_out_13 : 1'bz;  // Controlled_Buffer controlled_buffer_4
  assign out_23 = EN ? n4_b_2_out_10 : 1'bz;  // Controlled_Buffer controlled_buffer_5
  assign out_24 = EN ? n4_b_2_out_11 : 1'bz;  // Controlled_Buffer controlled_buffer_6
  assign out_25 = EN ? n4_b_2_out_12 : 1'bz;  // Controlled_Buffer controlled_buffer_7
  assign out_26 = EN ? n4_b_2_out_13 : 1'bz;  // Controlled_Buffer controlled_buffer_8

  // Other names for the same wires on the sheet: ENABLE = EN; R0 = out_19; R1 = out_20; R2 = out_21; R3 = out_22;
  //   R4 = out_23; R5 = out_24; R6 = out_25; R7 = out_26

  // Notes on the sheet:
  //   REGISTER A
  //   REGISTER B
  //   RESULT
  //   ALU
endmodule
